# Fritzing sketch HC06_LEDs_DHT (saved by Fritzing 0.9.3b)
breadboards: 1

parts:
  BT1 = Bluetooth HC-06d [package=THT]
  부품1 = Arduino Uno (Rev3)
  R1 = Resistor [tolerance=±5% resistance=220 package=THT]
  LED1 = LED - 5mm [color="Yellow (595nm)" package="5 mm [THT]"]
  LED2 = LED - 5mm [color="Green (555nm)" package="5 mm [THT]"]
  LED3 = LED - 5mm [color="Red (633nm)" package="5 mm [THT]"]
  R2 = Resistor [tolerance=±5% resistance=220 package=THT]
  R3 = Resistor [tolerance=±5% resistance=220 package=THT]
  DHT1 = Humidity and Temperature Sensor DHT11

nets:
  VCC: BT1.VCC, 부품1.5V, DHT1.Vcc
  GND: BT1.GND, 부품1.GND, R1.Pin_1, R2.Pin_1, R3.Pin_1, DHT1.GND_1
  N1: BT1.TXD, 부품1.D2
  N2: BT1.RXD, 부품1.D3_PWM
  N3: 부품1.D8, DHT1.Data-signal
  N4: 부품1.D5_PWM, LED3.anode
  N5: 부품1.D6_PWM, LED2.anode
  N6: 부품1.D7, LED1.anode
  N7: R1.Pin_0, LED1.cathode
  N8: LED2.cathode, R2.Pin_0
  N9: LED3.cathode, R3.Pin_0

custom parts:
  Bluetooth HC-06d: Bluetooth HC-06 - face down, pins down 16.5mm x 37.5mm PCB
  Humidity and Temperature Sensor DHT11: Digital relative humidity & temperature sensor DHT11
