# Fritzing sketch HC06_Only (saved by Fritzing 0.9.3b)
breadboards: 1

parts:
  BT1 = Bluetooth HC-06d [package=THT]
  부품1 = Arduino Uno (Rev3)

nets:
  VCC: BT1.VCC, 부품1.5V
  GND: BT1.GND, 부품1.GND
  N1: BT1.TXD, 부품1.D2
  N2: BT1.RXD, 부품1.D3_PWM

custom parts:
  Bluetooth HC-06d: Bluetooth HC-06 - face down, pins down 16.5mm x 37.5mm PCB
